# Fritzing sketch RotaryDecoder (saved by Fritzing 0.9.3b)
circuit board: 8.46667cm x 5.64444cm
breadboards: 1

parts:
  RE1 = Rotary Encoder [package=THT]
  Nano = Arduino Nano (Rev3.0) (ICSP)

nets:
  N1: RE1.EncoderPinA, Nano.D2
  N2: RE1.EncoderPinC, Nano.GND
  N3: RE1.EncoderPinB, Nano.D3
